# Fritzing sketch OpenCanSat (saved by Fritzing 1.0.8)
breadboards: 1

parts:
  A1 = Werner Rothschopf (modified to ESP32-S3-DevKitC dual USB by vanepp Aug 2024)
  M1 = BME280
  부품1 = InvenSense MPU6050
  A2 = NEO-6M GPS Module [part_number=GY-GPS6MV2]

nets:
  VCC: A1.Pin_1, A1.Pin_2, M1.VIN, 부품1.VCC, A2.Vcc
  N1: A1.Pin_12, M1.SDA, 부품1.SDA
  N2: A1.Pin_15, M1.SCL, 부품1.SCL
  GND: A1.Pin_22, A1.Pin_24, A1.Pin_44, M1.GND, 부품1.GND, A2.GND
  N3: A1.Pin_42, A2.Tx
  N4: A1.Pin_43, A2.Rx

custom parts:
  Werner Rothschopf (modified to ESP32-S3-DevKitC dual USB by vanepp Aug 2024): ESP32-S3 ESP32-S3-DevKitC-1 Dual USB development board Pyboard CircuitPython Micropython wifi BLE5.0 ESP32-S3.
  BME280: Temperature Humidity Barometric presure Sensor
  NEO-6M GPS Module: GY-GPS6MV2 NEO-6M GPS Module Module based on U-blox NEO-6M GPS engine, incorporating regulator for 3.3-5V DC input, MS621FE-compatible rechargeable battery for backup and EEPROM for storing configuration settings. Links: NEO-6 series product information page NEO-6 Datasheet
